// Digital circuit Mux with mistake.dig as structural Verilog
module Mux_with_mistake (
  input  a,
  input  b,
  input  sel,
  output out
);

  wire and_1_out, and_2_out, not_1_out;

  not not_1 (not_1_out, sel);
  and and_1 (and_1_out, a, sel);
  and and_2 (and_2_out, b, not_1_out);
  or or_1 (out, and_1_out, and_2_out);
endmodule
