// Digital circuit Xor.dig as structural Verilog
module Xor (
  input  a,
  input  b,
  output out_3
);

  wire and_1_out, not_1_out, or_1_out, or_2_out;

  and and_1 (and_1_out, a, b);
  or or_1 (or_1_out, b, a);
  not not_1 (not_1_out, or_1_out);
  or or_2 (or_2_out, and_1_out, not_1_out);
  not not_2 (out_3, or_2_out);
endmodule
